# Fritzing sketch water tank (saved by Fritzing 0.9.3b)
breadboards: 1

parts:
  U1 = ESP32-38PinWide [part_number=ESP32-38PinWide]
  hc-sr1 = hc-sr04
  SERVO1 = Tower Pro SG90 servo [part_number=101246]
  LED1 = smd LED [color="Yellow (592nm)" package="0805 [SMD]"]
  LED2 = smd LED [color="Red (633nm)" package="0805 [SMD]"]
  LED3 = smd LED [color="Green (570nm)" package="0805 [SMD]"]
  R3 = Resistor [tolerance=±5% resistance=100 package="1206 [SMD]"]
  R7 = Resistor [tolerance=±5% resistance=100 package="1206 [SMD]"]
  C1 = Tantalum Capacitor [capacitance=1μF package="100 mil [THT, tantalum]"]
  R8 = Resistor [tolerance=±5% resistance=100 package="1206 [SMD]"]
  R9 = Resistor [tolerance=±5% resistance=100 package="1206 [SMD]"]

nets:
  N1: U1.GPIO25, SERVO1.Signal
  N2: U1.GPIO26, LED3.anode
  N3: U1.GPIO27, LED1.anode
  N4: U1.GPIO13, LED2.anode
  GND: U1.GPIO11, hc-sr1.GND, SERVO1.GND, R3.Pin_0, C1.-, R8.Pin_0, R9.Pin_0
  VIN: U1.VIN, hc-sr1.VCC, SERVO1.+5V, R7.Pin_0
  N5: U1.GPIO5, hc-sr1.Trig
  N6: U1.GPIO18, hc-sr1.Echo
  N7: LED1.cathode, R9.Pin_1
  N8: LED2.cathode, R3.Pin_1
  N9: LED3.cathode, R8.Pin_1
  N10: R7.Pin_1, C1.+

custom parts:
  ESP32-38PinWide: Generic 38-Pin ESP32 with wide format (only access to one side of pins on a breadboard) based on Stephen Lilley's HiLetgo ESP-WROOM-32 ESP32 ESP-32S Development Board.
  Tower Pro SG90 servo: Original file by John De Cristofaro http://www.adafruit.com/products/1449 Adafruit Feedback Servo (Small) Edited by: e-radionica.com 28/9/2015
